// Logisim project Branch Control.circ as structural Verilog: 1 circuit, main circuit Branch-Control
module Branch_Control (
  input  [31:0] in_1,
  input  [31:0] in_2,
  input  [31:0] in_3,
  input  [25:0] in_4,
  input  [1:0] Selector,
  input  [15:0] in_6,
  output [31:0] PC_prime
);

  wire comparator_1_eq, RS_0, RS__0, RS__RT;
  wire [13:0] bit_extender_1_out;
  wire [31:0] PC_4, PC_4_x;

  Comparator #(.width(32)) comparator_1 (.a(in_1), .b({32{1'b0}}), .eq(comparator_1_eq), .lt(RS_0));  // open: gt
  Comparator #(.width(32)) comparator_2 (.a(in_1), .b(in_2), .eq(RS__RT));  // open: gt, lt
  Adder #(.width(32)) adder_1 (.a(in_3), .b(32'h4), .out(PC_4));  // open: cin, cout
  assign bit_extender_1_out = {{13{in_6[15]}}, in_6[15]};  // Bit_Extender bit_extender_1
  or or_1 (RS__0, comparator_1_eq, RS_0);
  Adder #(.width(32)) adder_2 (.a(PC_4), .b({bit_extender_1_out, in_6, 2'b00}), .out(PC_4_x));  // open: cin, cout
  Multiplexer #(.select(2), .width(32), .enable("false")) multiplexer_1 (
    .in0(PC_4), .in1(PC_4_x), .in2({in_3[31:28], in_4, 2'b00}), .in3(in_1), .out(PC_prime), .sel(Selector));

  // Other names for the same wires on the sheet: offset[15:0] = in_6; dest[25:0] = in_4;
  //   jmp[31:2] = {in_3[31:28], in_4}; PC[31:0] = in_3; RS[31:0] = in_1; RT[31:0] = in_2

  // Notes on the sheet:
  //   Branch Control
endmodule
