// Logisim project Data-Path.circ as structural Verilog: 1 circuit, main circuit main
module main (
  input  [6:0] Keyboard,
  input  [31:0] RAM_data,
  input  [15:0] constante,
  input  Enable_Hi_Lo,
  input  [4:0] Data_Adress,
  input  R_W,
  input  [4:0] Selector_A,
  input  store_word,
  input  [4:0] Selector_B,
  input  KBD_AVAILABLE,
  input  [2:0] RF_input_selector,
  input  Type_I,
  input  [3:0] ALU_Op__Selector,
  input  Reset,
  input  Const_extender_selector,
  input  Clock,
  output [31:0] Dir_Address,
  output [6:0] tty_DATA,
  output [31:0] RAM_write_data
);

  wire [31:0] alu_1_high, alu_input_1_b, ALU_out, High_out, Low_out, main_1_rf_input, RS, Rs_t, RT, Rt_t, SP;

  Register_File_Input_main main_1 (
    .RAM(RAM_data), .ALU_Output(ALU_out), .Keyboard(Keyboard), .High(High_out),
    .KBD_available(KBD_AVAILABLE), .Low(Low_out), .RF_Input(main_1_rf_input), .Selector(RF_input_selector),
    .clock(Clock));
  ALU_Input alu_input_1 (
    .Rt(RT), .Const(constante), .B(alu_input_1_b), .Const_Extender_Selector(Const_extender_selector),
    .Type_I(Type_I));
  ALU alu_1 (.Data_A(RS), .Data_B(alu_input_1_b), .ALU_Output(ALU_out), .High(alu_1_high), .Selector(ALU_Op__Selector));
  // Register_File_main main_2: pin names not known; wires that end beside it: R_W, main_1_rf_input, R_W, Data_Adress, Clock, Selector_A, Selector_B, Reset, RS, RT, SP
  Multiplexer #(.width(32), .enable("false")) multiplexer_1 (
    .in0(Rs_t), .in1(Rt_t), .out(RAM_write_data), .sel(store_word));

  // Other names for the same wires on the sheet: CES = Const_extender_selector; Clk = Clock; const[15:0] = constante;
  //   DA[4:0] = Data_Adress; E_HL = Enable_Hi_Lo; KBD_AVAIL = KBD_AVAILABLE; Kbd_data[6:0] = Keyboard;
  //   op[3:0] = ALU_Op__Selector; RAM__w[31:0] = RAM_write_data; RAM_d[31:0] = RAM_data;
  //   RF_sel[2:0] = RF_input_selector; Rst = Reset; SA[4:0] = Selector_A; SB[4:0] = Selector_B; sw = store_word

  // Notes on the sheet:
  //   Inputs
  //   Outputs
endmodule
